# Fritzing sketch Clock (saved by Fritzing 0.9.3b)
breadboards: 1

parts:
  7SEG1 = 7-Segment LED I2C Backpack (white)
  Деталь1 = Arduino Nano (Rev3.0)
  S1 = Pushbutton [part_number=buttonPin package="[SMD]"]
  S2 = Pushbutton [part_number=buttonPinDisable package="[SMD]"]
  RTC1 = DS3231 AT24C32 Real Time Clock
  U2 = RELAY-SOLIDSTATE [package=relay-s108t02]
  FC-1 = Sound Sensor

nets:
  VCC: 7SEG1.V+, Деталь1.5V, RTC1.VCC, U2.+, FC-1.VCC
  GND: 7SEG1.GND, Деталь1.GND, Деталь1.D10, Деталь1.D11/MOSI, S1.Pin_1, S1.Pin_2, S2.Pin_1, S2.Pin_2, RTC1.GND, U2.-, FC-1.GND
  N1: 7SEG1.SDA, Деталь1.D8
  N2: 7SEG1.SCL, Деталь1.D9
  N3: Деталь1.D4, U2.T2
  N4: Деталь1.A5, RTC1.SCL
  N5: Деталь1.A4, RTC1.SDA
  N6: Деталь1.A0, FC-1.OUT

custom parts:
  7-Segment LED I2C Backpack (white): 4-digit, 7-segment LED Display with I2C Control
  DS3231 AT24C32 Real Time Clock: Real-time clock basedo on chip DS3231, plus memory chip AT24C32 (32 Kb storage capacity). On-chip temperature sensor with an accuracy of ±3 ℃, I2C bus interface maximum speed: 400 kHz. Operating voltage: 3.3 V to 5.5 V with battery backup capabilities.
