# Fritzing sketch ModelFurious (saved by Fritzing 0.9.3b)
breadboards: 1

parts:
  S1 = H-Bridge with L298N
  BAT1 = BC9VPC [package=bc9vpc]
  S2 = Square Pushbutton
  Деталь2 = NRF24L01+ Breakout Board
  M3 = DC Motor
  M4 = DC Motor
  Деталь3 = Arduino Nano (Rev3.0)
  S3 = H-Bridge with L298N
  M5 = DC Motor
  M6 = DC Motor

nets:
  12V: S1.12V, S2.leg1, Деталь3.VIN
  GND: S1.GND, BAT1.V-, Деталь2.GND, Деталь3.GND
  5V: S1.5V, Деталь2.VCC
  N1: S1.ENA, Деталь3.D9
  N2: S1.IN1, Деталь3.D2
  N3: S1.IN2, Деталь3.D4
  N4: S1.IN3, Деталь3.D7
  N5: S1.IN4, Деталь3.D8
  N6: S1.ENB, Деталь3.D10
  N7: S1.M1-01, M3.pin_2
  N8: S1.M1-02, M3.pin_1
  N9: S1.M2-01, M4.pin_2
  N10: S1.M2-02, M4.pin_1
  N11: BAT1.V+, S2.leg0
  N12: Деталь2.CE, Деталь3.A0
  N13: Деталь2.CS, Деталь3.A1
  N14: Деталь2.SCK, Деталь3.D13/SCK
  N15: Деталь2.MOSI, Деталь3.D11/MOSI
  N16: Деталь2.MISO, Деталь3.D12/MISO
  N17: Деталь3.D5, S3.ENA
  N18: Деталь3.D6, S3.ENB
  N19: Деталь3.A5, S3.IN4
  N20: Деталь3.A4, S3.IN3
  N21: Деталь3.A3, S3.IN2
  N22: Деталь3.A2, S3.IN1
  N23: S3.M1-01, M6.pin_2
  N24: S3.M1-02, M6.pin_1
  N25: S3.M2-01, M5.pin_2
  N26: S3.M2-02, M5.pin_1

custom parts:
  H-Bridge with L298N: h-bridge
