# Fritzing sketch ModelGrasshopper (saved by Fritzing 0.9.3b)
breadboards: 2

parts:
  S1 = H-Bridge with L298N
  BAT1 = BC9VPC [package=bc9vpc]
  S2 = Square Pushbutton
  Деталь2 = NRF24L01+ Breakout Board
  U1 = TRANSCHIPTC5747 [package=camera_sfv24r-2st_2]
  M3 = DC Motor
  M4 = DC Motor
  Деталь3 = Arduino Nano (Rev3.0)
  J1 = Screw terminal - 2 pins [package=THT]
  R1 = Resistor [tolerance=±5% resistance=7.5k package="2512 [SMD]"]
  R2 = Resistor [tolerance=±5% resistance=33k package=THT]
  S3 = H-Bridge with L298N
  M5 = DC Motor
  M6 = DC Motor
  S4 = H-Bridge with L298N
  M7 = DC Motor
  M8 = DC Motor
  J2 = Basic Servo [part_number="Head Servo"]
  J3 = Basic Servo [part_number="Head Servo"]

nets:
  12V: S1.12V, S2.leg1, Деталь3.VIN, S3.12V, S4.12V
  GND: S1.GND, BAT1.V-, Деталь2.GND, U1.AVDD28, Деталь3.GND, J1.pin2, R1.Pin_0, S3.GND, S4.GND, J2.gnd
  5V: S1.5V, Деталь2.VCC
  N1: S1.ENA, Деталь3.D5, S3.ENA, S4.ENA
  N2: S1.IN1, Деталь3.D2, S3.IN1, S4.IN1
  N3: S1.IN2, Деталь3.D4, S3.IN2, S4.IN2
  N4: S1.IN3, Деталь3.D7, S3.IN3, S4.IN3
  N5: S1.IN4, Деталь3.D8, S3.IN4, S4.IN4
  N6: S1.ENB, Деталь3.D6, S3.ENB, S4.ENB
  N7: S1.M1-01, M3.pin_2
  N8: S1.M1-02, M3.pin_1
  N9: S1.M2-01, M4.pin_2
  N10: S1.M2-02, M4.pin_1
  N11: BAT1.V+, S2.leg0
  N12: Деталь2.CE, Деталь3.A0
  N13: Деталь2.CS, Деталь3.A1
  N14: Деталь2.SCK, Деталь3.D13/SCK
  N15: Деталь2.MOSI, Деталь3.D11/MOSI
  N16: Деталь2.MISO, Деталь3.D12/MISO
  5V_2: U1.SCLK, S4.5V, J2.vcc
  N17: Деталь3.D9, J3.pulse
  N18: Деталь3.D10, J2.pulse
  N19: Деталь3.A2, R1.Pin_1, R2.Pin_1
  N20: J1.pin1, R2.Pin_0
  5V_3: S3.5V, J3.vcc
  N21: S3.M1-01, M6.pin_2
  N22: S3.M1-02, M6.pin_1
  N23: S3.M2-01, M5.pin_2
  N24: S3.M2-02, M5.pin_1
  N25: S4.M1-01, M8.pin_2
  N26: S4.M1-02, M8.pin_1
  N27: S4.M2-01, M7.pin_2
  N28: S4.M2-02, M7.pin_1

custom parts:
  H-Bridge with L298N: h-bridge
