# Fritzing sketch ModelR-v1 (saved by Fritzing 0.9.3b)
breadboards: 1

parts:
  Деталь1 = Arduino Uno (Rev3)
  S1 = H-Bridge with L298N
  M1 = DC Motor
  M2 = DC Motor
  BAT1 = BC9VPC [package=bc9vpc]
  hc-sr1 = hc-sr04
  U1 = Voltage Regulator - 5V [package="TO220 [THT]"]
  J1 = Basic Servo [part_number="Head Servo"]
  J2 = Basic Servo [part_number="Claw Servo"]
  J3 = Basic Servo [part_number="Hand Servo"]
  S2 = Square Pushbutton
  Деталь2 = NRF24L01+ Breakout Board
  J4 = Piezo Speaker [part_number=Cooler]
  J5 = Basic Force Sensing Resistor (FSR) [package=THT]
  R1 = Resistor [tolerance=±5% resistance=10k package="2512 [SMD]"]

nets:
  N1: Деталь1.A0, Деталь2.CE
  N2: Деталь1.A1, Деталь2.CS
  N3: Деталь1.A2, hc-sr1.Trig
  N4: Деталь1.A3, hc-sr1.Echo
  N5: Деталь1.A4/SDA, J5.pin_1
  N6: Деталь1.D8, S1.IN4
  N7: Деталь1.D9_PWM, J1.pulse
  N8: Деталь1.D10_PWM/SS, J2.pulse
  N9: Деталь1.D11_PWM/MOSI, Деталь2.MOSI
  N10: Деталь1.D12/MISO, Деталь2.MISO
  N11: Деталь1.D13/SCK, Деталь2.SCK
  GND: Деталь1.GND, S1.GND, BAT1.V-, hc-sr1.GND, J1.gnd, J2.gnd, J3.gnd, Деталь2.GND, J4.pin1, R1.Pin_0
  N12: Деталь1.D2, S1.IN1
  N13: Деталь1.D3_PWM, J3.pulse
  N14: Деталь1.D4, S1.IN2
  N15: Деталь1.D5_PWM, S1.ENA
  N16: Деталь1.D6_PWM, S1.ENB
  N17: Деталь1.D7, S1.IN3
  VCC: Деталь1.5V, hc-sr1.VCC, J1.vcc, Деталь2.VCC, J4.pin2, J5.pin_0
  VIN: Деталь1.VIN, S1.12V, U1.input_voltage, S2.leg1
  5V: S1.5V, J2.vcc
  N18: S1.M1-01, M2.pin_2
  N19: S1.M1-02, M2.pin_1
  N20: S1.M2-01, M1.pin_2
  N21: S1.M2-02, M1.pin_1
  N22: BAT1.V+, S2.leg0

custom parts:
  H-Bridge with L298N: h-bridge
