# Fritzing sketch ModelS (saved by Fritzing 0.9.3b)
breadboards: 2

parts:
  S1 = H-Bridge with L298N
  M1 = DC Motor
  M2 = DC Motor
  BAT1 = BC9VPC [package=bc9vpc]
  S2 = Square Pushbutton
  Деталь2 = NRF24L01+ Breakout Board
  IC1 = Voltage Regulator [package=78xxl]
  IC2 = Voltage Regulator [package=78xxl]
  U1 = TRANSCHIPTC5747 [package=camera_sfv24r-2st_2]
  M3 = DC Motor
  M4 = DC Motor
  Деталь3 = Arduino Nano (Rev3.0)
  J1 = Screw terminal - 2 pins [package=THT]
  R1 = Resistor [tolerance=±5% resistance=7.5k package="2512 [SMD]"]
  R2 = Resistor [tolerance=±5% resistance=33k package=THT]

nets:
  12V: S1.12V, S2.leg1, IC1.IN, IC2.IN, Деталь3.VIN
  GND: S1.GND, BAT1.V-, Деталь2.GND, IC1.GND, IC2.GND, U1.AVDD28, Деталь3.GND, J1.pin2, R1.Pin_0
  N1: S1.ENA, Деталь3.D5
  N2: S1.IN1, Деталь3.D2
  N3: S1.IN2, Деталь3.D4
  N4: S1.IN3, Деталь3.D7
  N5: S1.IN4, Деталь3.D8
  N6: S1.ENB, Деталь3.D6
  N7: S1.M1-01, M2.pin_2, M3.pin_2
  N8: S1.M1-02, M2.pin_1, M3.pin_1
  N9: S1.M2-01, M1.pin_2, M4.pin_2
  N10: S1.M2-02, M1.pin_1, M4.pin_1
  N11: BAT1.V+, S2.leg0
  N12: Деталь2.VCC, IC1.OUT
  N13: Деталь2.CE, Деталь3.A0
  N14: Деталь2.CS, Деталь3.A1
  N15: Деталь2.SCK, Деталь3.D13/SCK
  N16: Деталь2.MOSI, Деталь3.D11/MOSI
  N17: Деталь2.MISO, Деталь3.D12/MISO
  N18: IC2.OUT, U1.SCLK
  N19: Деталь3.A2, R1.Pin_1, R2.Pin_1
  N20: J1.pin1, R2.Pin_0

custom parts:
  H-Bridge with L298N: h-bridge
