# Fritzing sketch ModelScorpio (saved by Fritzing 0.9.3b)
breadboards: 2

parts:
  S1 = H-Bridge with L298N
  BAT1 = BC9VPC [package=bc9vpc]
  S2 = Square Pushbutton
  Деталь2 = NRF24L01+ Breakout Board
  U1 = TRANSCHIPTC5747 [package=camera_sfv24r-2st_2]
  M3 = DC Motor
  M4 = DC Motor
  Деталь3 = Arduino Nano (Rev3.0)
  J1 = Screw terminal - 2 pins [package=THT]
  R1 = Resistor [tolerance=±5% resistance=7.5k package="2512 [SMD]"]
  R2 = Resistor [tolerance=±5% resistance=33k package=THT]
  hc-sr2 = hc-sr04

nets:
  12V: S1.12V, S2.leg1, Деталь3.VIN
  GND: S1.GND, BAT1.V-, Деталь2.GND, U1.AVDD28, Деталь3.GND, J1.pin2, R1.Pin_0, hc-sr2.GND
  5V: S1.5V, Деталь2.VCC
  N1: S1.ENA, S1.ENB, Деталь3.D5
  N2: S1.IN1, Деталь3.D2
  N3: S1.IN2, Деталь3.D4
  N4: S1.IN3, Деталь3.D7
  N5: S1.IN4, Деталь3.D8
  N6: S1.M1-01, M3.pin_2
  N7: S1.M1-02, M3.pin_1
  N8: S1.M2-01, M4.pin_2
  N9: S1.M2-02, M4.pin_1
  N10: BAT1.V+, S2.leg0
  N11: Деталь2.CE, Деталь3.A0
  N12: Деталь2.CS, Деталь3.A1
  N13: Деталь2.SCK, Деталь3.D13/SCK
  N14: Деталь2.MOSI, Деталь3.D11/MOSI
  N15: Деталь2.MISO, Деталь3.D12/MISO
  5V_2: U1.SCLK, Деталь3.5V, hc-sr2.VCC
  N16: Деталь3.A4, hc-sr2.Echo
  N17: Деталь3.A3, hc-sr2.Trig
  N18: Деталь3.A2, R1.Pin_1, R2.Pin_1
  N19: J1.pin1, R2.Pin_0

custom parts:
  H-Bridge with L298N: h-bridge
