# Fritzing sketch ModelT (saved by Fritzing 0.9.3b)
breadboards: 3

parts:
  Деталь1 = Arduino Uno (Rev3)
  S1 = H-Bridge with L298N
  M1 = DC Motor
  M2 = DC Motor
  BAT1 = BC9VPC [package=bc9vpc]
  S2 = Square Pushbutton
  Деталь2 = NRF24L01+ Breakout Board
  Деталь3 = Arduino Nano (Rev3.0)
  S3 = H-Bridge with L298N
  M3 = DC Motor
  M4 = DC Motor
  R3 = Resistor [tolerance=±5% resistance=33k package=THT]
  R4 = Resistor [tolerance=±5% resistance=7.5k package="2512 [SMD]"]
  J2 = Screw terminal - 2 pins [package=THT]
  U2 = TRANSCHIPTC5747 [package=camera_sfv24r-2st_2]
  IC3 = Voltage Regulator [package=78xxl]
  J3 = Basic Servo
  Деталь4 = Adafruit VL53L0X Time of Flight Distance Sensor [part_number="Adafruit #3317"]
  J4 = Basic Servo
  J5 = Basic Servo
  J6 = Basic Servo
  J7 = Basic Servo
  J8 = Basic Servo
  J9 = Basic Servo
  IC4 = Voltage Regulator [package=78xxl]
  IC5 = Voltage Regulator [package=78xxl]
  IC6 = Voltage Regulator [package=78xxl]
  IC7 = Voltage Regulator [package=78xxl]
  IC8 = Voltage Regulator [package=78xxl]

nets:
  N1: Деталь1.A0, Деталь2.CE
  N2: Деталь1.A1, Деталь2.CS
  N3: Деталь1.A2, R3.Pin_1, R4.Pin_1
  N4: Деталь1.A4/SDA, Деталь4.SDA
  N5: Деталь1.A5/SCL, Деталь4.SCL
  N6: Деталь1.D8, S1.IN4, S3.IN4
  N7: Деталь1.D9_PWM, J3.pulse
  N8: Деталь1.D11_PWM/MOSI, Деталь2.MOSI
  N9: Деталь1.D12/MISO, Деталь2.MISO
  N10: Деталь1.D13/SCK, Деталь2.SCK
  GND: Деталь1.GND, S1.GND, BAT1.V-, Деталь2.GND, Деталь3.GND, S3.GND, R4.Pin_0, J2.pin2, U2.AVDD28, IC3.GND, J3.gnd, Деталь4.GND, J4.gnd, J5.gnd, J7.gnd, J8.gnd, J9.gnd, IC4.GND, IC5.GND, IC6.GND, IC7.GND, IC8.GND
  N11: Деталь1.D0/RX, Деталь3.D1/TX
  N12: Деталь1.D1/TX, Деталь3.D0/RX
  N13: Деталь1.D2, S1.IN1, S3.IN1
  N14: Деталь1.D4, S1.IN2, S3.IN2
  N15: Деталь1.D5_PWM, S1.ENA, S3.ENA
  N16: Деталь1.D6_PWM, S1.ENB, S3.ENB
  N17: Деталь1.D7, S1.IN3, S3.IN3
  5V: Деталь1.5V, Деталь4.VIN
  VIN: Деталь1.VIN, S1.12V, S2.leg1, Деталь3.VIN, S3.12V, IC3.IN, IC4.IN, IC5.IN, IC6.IN, IC7.IN, IC8.IN
  5V_2: S1.5V, J3.vcc
  N18: S1.M1-01, M2.pin_2
  N19: S1.M1-02, M2.pin_1
  N20: S1.M2-01, M1.pin_2
  N21: S1.M2-02, M1.pin_1
  N22: BAT1.V+, S2.leg0
  N23: Деталь2.VCC, IC3.OUT
  N24: Деталь3.D2, J9.pulse
  N25: Деталь3.D3, J8.pulse
  N26: Деталь3.D4, J7.pulse
  N27: Деталь3.D5, J6.pulse
  N28: Деталь3.D6, J5.pulse
  N29: Деталь3.D7, J4.pulse
  N30: S3.5V, U2.SCLK
  N31: S3.M1-01, M4.pin_2
  N32: S3.M1-02, M4.pin_1
  N33: S3.M2-01, M3.pin_2
  N34: S3.M2-02, M3.pin_1
  N35: R3.Pin_0, J2.pin1
  N36: J4.vcc, IC4.OUT
  N37: J5.vcc, IC5.OUT
  N38: J6.vcc, IC6.OUT
  VCC: J7.vcc, J9.vcc, IC8.OUT
  N39: J8.vcc, IC7.OUT

custom parts:
  H-Bridge with L298N: h-bridge
  Adafruit VL53L0X Time of Flight Distance Sensor: The VL53L0X is a Time of Flight distance sensor like no other you've used! The sensor contains a very tiny invisible laser source, and a matching sensor. The VL53L0X can detect the "time of flight", or how long the light has taken to bounce back to the sensor. Since it uses a very narrow light source, it is good for determining distance of only the surface directly in front of it. Unlike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
