# Fritzing sketch Transmitter (saved by Fritzing 0.9.3b)
breadboards: 2

parts:
  BAT1 = BC9VPC [package=bc9vpc]
  S2 = Square Pushbutton
  Деталь2 = NRF24L01+ Breakout Board
  Деталь3 = Arduino Nano (Rev3.0)
  Grove1 = Grove OLED 128x96
  U1 = POT [package=pot_mammoth]
  Деталь4 = Thumb Joystick
  S3 = Pushbutton [package="[SMD]"]
  S4 = Pushbutton [package="[SMD]"]
  S5 = Pushbutton [package="[SMD]"]
  S6 = Pushbutton [package="[SMD]"]

nets:
  N1: BAT1.V+, S2.leg0
  GND: BAT1.V-, Деталь3.GND, Grove1.GND, U1.E, Деталь4.GND, S3.Pin_1, S3.Pin_2, S4.Pin_1, S4.Pin_2, S5.Pin_1, S5.Pin_2, S6.Pin_1, S6.Pin_2
  N2: S2.leg1, Деталь3.VIN
  VCC: Деталь2.VCC, Деталь3.5V, U1.S, Деталь4.VCC
  N3: Деталь2.CE, Деталь3.A2
  N4: Деталь2.CS, Деталь3.A3
  N5: Деталь2.SCK, Деталь3.D13/SCK
  N6: Деталь2.MOSI, Деталь3.D11/MOSI
  N7: Деталь2.MISO, Деталь3.D12/MISO
  N8: Деталь3.D4, S6.Pin_4
  N9: Деталь3.D5, S5.Pin_4
  N10: Деталь3.D6, S4.Pin_4
  N11: Деталь3.D7, S3.Pin_3, S3.Pin_4
  N12: Деталь3.D8, Деталь4.SEL
  N13: Деталь3.A6, U1.A
  N14: Деталь3.A5, Grove1.SCL
  N15: Деталь3.A4, Grove1.SDA
  N16: Деталь3.A1, Деталь4.HORZ
  N17: Деталь3.A0, Деталь4.VERT
  3V3: Деталь3.3V3, Grove1.VCC
